// Logisim project CPU_Design.circ as structural Verilog: 6 circuits, main circuit main
module main (
  input  PCWrite,
  input  InstrWrite,
  input  InstrRead,
  output [5:0] Func,
  output [7:0] Result,
  output [7:0] ImmediateValue,
  output [7:0] out_7,
  output [7:0] out_8,
  output [7:0] out_9,
  output [7:0] out_10,
  output [3:0] OPCODE
);

  wire alu_1_zero, and_1_out, clock_1_out, clock_2_out, clock_3_out, controlunit_1_alusource,
       controlunit_1_branch, controlunit_1_jump, controlunit_1_memtoreg, controlunit_1_memwrite,
       controlunit_1_registerdest, controlunit_1_registerwrite, Reset_out;
  wire [1:0] multiplexer_3_out;
  wire [2:0] controlunit_1_alucontrol;
  wire [7:0] datamemory_1_readdata, multiplexer_4_out, multiplexer_5_out, registerfile_1_rd1,
       registerfile_1_rd2;
  wire [11:8] instructionmemory_1_instructionoutput;
  wire [15:0] adder_1_out, bit_extender_1_out, INSTRROM_data, multiplexer_1_out, multiplexer_2_out,
       register_1_q;

  Button Reset (.out(Reset_out));
  Multiplexer #(.width(16)) multiplexer_1 (
    .in0(16'h1), .in1(bit_extender_1_out), .out(multiplexer_1_out), .sel(and_1_out));
  Multiplexer #(.width(16)) multiplexer_2 (
    .in0(adder_1_out), .in1({registerfile_1_rd2, registerfile_1_rd1}), .out(multiplexer_2_out),
    .sel(controlunit_1_jump));
  Clock clock_1 (.out(clock_1_out));
  ROM #(.addrWidth(16), .dataWidth(16)) INSTRROM (.addr(register_1_q), .data(INSTRROM_data));
  Register #(.width(16)) register_1 (
    .D(multiplexer_2_out), .en(PCWrite), .clk(clock_1_out), .Q(register_1_q), .clr(Reset_out));
  Adder #(.width(16)) adder_1 (.a(multiplexer_1_out), .b(register_1_q), .out(adder_1_out));  // open: cin, cout
  InstructionMemory instructionmemory_1 (
    .InstrAddress(register_1_q), .WriteEnable(InstrWrite), .DataIn(INSTRROM_data), .ReadEnable(InstrRead),
    .Clock(clock_1_out),
    .InstructionOutput({OPCODE, instructionmemory_1_instructionoutput, ImmediateValue[7:6], Func}));
  Clock clock_2 (.out(clock_2_out));
  Multiplexer #(.width(2)) multiplexer_3 (
    .in0(ImmediateValue[7:6]), .in1(instructionmemory_1_instructionoutput[9:8]), .out(multiplexer_3_out),
    .sel(controlunit_1_registerdest));
  assign bit_extender_1_out = {{8{ImmediateValue[7]}}, {ImmediateValue[7:6], Func}};  // Bit_Extender bit_extender_1
  ControlUnit controlunit_1 (
    .OpCode(OPCODE), .Func(Func), .RegisterDest(controlunit_1_registerdest),
    .ALUSource(controlunit_1_alusource), .RegisterWrite(controlunit_1_registerwrite),
    .MemWrite(controlunit_1_memwrite), .MemToReg(controlunit_1_memtoreg),
    .ALUControl(controlunit_1_alucontrol), .Branch(controlunit_1_branch), .Jump(controlunit_1_jump));
  RegisterFile registerfile_1 (
    .A1(instructionmemory_1_instructionoutput[11:10]), .A2(instructionmemory_1_instructionoutput[9:8]),
    .WriteData3(multiplexer_5_out), .Clock(clock_2_out), .WriteEnable(controlunit_1_registerwrite),
    .A3(multiplexer_3_out), .Reset(Reset_out), .RegisterZeroDisplay(out_7), .RD1(registerfile_1_rd1),
    .RegisterADisplay(out_8), .RegisterBDisplay(out_9), .RD2(registerfile_1_rd2), .RegisterCDisplay(out_10));
  Multiplexer #(.width(8)) multiplexer_4 (
    .in0(registerfile_1_rd2), .in1({ImmediateValue[7:6], Func}), .out(multiplexer_4_out),
    .sel(controlunit_1_alusource));
  Clock clock_3 (.out(clock_3_out));
  ALU alu_1 (
    .SrcA(registerfile_1_rd1), .SrcB(multiplexer_4_out), .AluSelect(controlunit_1_alucontrol),
    .Result(Result), .Zero(alu_1_zero));
  DataMemory datamemory_1 (
    .Address(Result), .WriteEnable(controlunit_1_memwrite), .Clock(clock_3_out),
    .WriteData(registerfile_1_rd2), .ReadData(datamemory_1_readdata));
  and and_1 (and_1_out, alu_1_zero, controlunit_1_branch);
  Multiplexer #(.width(8)) multiplexer_5 (
    .in0(Result), .in1(datamemory_1_readdata), .out(multiplexer_5_out), .sel(controlunit_1_memtoreg));

  assign ImmediateValue[5:0] = Func;

  // Notes on the sheet:
  //   contents of INSTRROM (hex, n*v repeats v):
  //   1b2 3f2
endmodule

module RegisterFile (
  input  [1:0] A1,
  input  [1:0] A2,
  input  [7:0] WriteData3,
  input  Clock,
  input  WriteEnable,
  input  [1:0] A3,
  input  Reset,
  output [7:0] RegisterZeroDisplay,
  output [7:0] RD1,
  output [7:0] RegisterADisplay,
  output [7:0] RegisterBDisplay,
  output [7:0] RD2,
  output [7:0] RegisterCDisplay
);

  wire and_1_out, and_2_out, and_3_out, decoder_1_out1, decoder_1_out2, decoder_1_out3;

  Decoder #(.select(2)) decoder_1 (
    .out1(decoder_1_out1), .out2(decoder_1_out2), .out3(decoder_1_out3), .sel(A3));  // open: out0, en
  and and_1 (and_1_out, WriteEnable, decoder_1_out1);
  and and_2 (and_2_out, WriteEnable, decoder_1_out2);
  and and_3 (and_3_out, WriteEnable, decoder_1_out3);
  Register ZeroReg (.D(WriteData3), .en(1'b0), .clk(Clock), .Q(RegisterZeroDisplay), .clr(Reset));
  Register RegisterA (.D(WriteData3), .en(and_1_out), .clk(Clock), .Q(RegisterADisplay), .clr(Reset));
  Register RegisterB (.D(WriteData3), .en(and_2_out), .clk(Clock), .Q(RegisterBDisplay), .clr(Reset));
  Register RegisterC (.D(WriteData3), .en(and_3_out), .clk(Clock), .Q(RegisterCDisplay), .clr(Reset));
  Multiplexer #(.select(2), .width(8)) multiplexer_1 (
    .in0(RegisterZeroDisplay), .in1(RegisterADisplay), .in2(RegisterBDisplay), .in3(RegisterCDisplay),
    .out(RD1), .sel(A1));
  Multiplexer #(.select(2), .width(8)) multiplexer_2 (
    .in0(RegisterZeroDisplay), .in1(RegisterADisplay), .in2(RegisterBDisplay), .in3(RegisterCDisplay),
    .out(RD2), .sel(A2));

  // Notes on the sheet:
  //   ZeroReg is ReadOnly
endmodule

module ALU (
  input  [7:0] SrcA,
  input  [7:0] SrcB,
  input  [2:0] AluSelect,
  output [7:0] Result,
  output Zero
);

  wire [7:0] adder_1_out, and_1_out, bit_extender_1_out, multiplexer_1_out, not_1_out, or_1_out;

  assign not_1_out = ~SrcB;  // NOT_Gate not_1, 8 bits wide
  Multiplexer #(.width(8)) multiplexer_1 (.in0(SrcB), .in1(not_1_out), .out(multiplexer_1_out), .sel(AluSelect[2]));
  assign and_1_out = SrcA & multiplexer_1_out;  // AND_Gate and_1, 8 bits wide
  assign or_1_out = SrcA | multiplexer_1_out;  // OR_Gate or_1, 8 bits wide
  Adder adder_1 (.a(SrcA), .b(multiplexer_1_out), .out(adder_1_out), .cin(AluSelect[2]));  // open: cout
  assign bit_extender_1_out = {{7{1'b0}}, adder_1_out[7]};  // Bit_Extender bit_extender_1
  Multiplexer #(.select(2), .width(8)) multiplexer_2 (
    .in0(and_1_out), .in1(or_1_out), .in2(adder_1_out), .in3(bit_extender_1_out), .out(Result),
    .sel(AluSelect[1:0]));
  nor nor_1 (Zero, Result[0], Result[1], Result[2], Result[3], Result[4], Result[5], Result[6], Result[7]);
endmodule

module ControlUnit (
  input  [3:0] OpCode,
  input  [5:0] Func,
  output RegisterDest,
  output ALUSource,
  output RegisterWrite,
  output MemWrite,
  output MemToReg,
  output [2:0] ALUControl,
  output Branch,
  output Jump
);

  wire decoder_1_out0, decoder_1_out1, decoder_1_out2, or_1_out, or_2_out;

  Decoder #(.select(3)) decoder_1 (
    .out0(decoder_1_out0), .out1(decoder_1_out1), .out2(decoder_1_out2), .out3(MemToReg), .out4(MemWrite),
    .out5(Branch), .out6(Jump), .sel(OpCode[2:0]));  // open: out7, en
  Multiplexer #(.select(3), .width(3)) multiplexer_1 (
    .in0(Func[2:0]), .in1(3'b010), .in2(3'b110), .in3(3'b010), .in4(3'b010), .in5(3'b110), .out(ALUControl),
    .sel(OpCode[2:0]));  // open: in6, in7
  or or_1 (or_1_out, MemWrite, decoder_1_out1, decoder_1_out2, MemToReg);
  or or_2 (or_2_out, decoder_1_out0, decoder_1_out1, decoder_1_out2, MemToReg);
  Multiplexer multiplexer_2 (.in0(1'b0), .in1(1'b1), .out(RegisterDest), .sel(or_1_out));
  Multiplexer multiplexer_3 (.in0(1'b0), .in1(1'b1), .out(ALUSource), .sel(or_1_out));
  Multiplexer multiplexer_4 (.in0(1'b0), .in1(1'b1), .out(RegisterWrite), .sel(or_2_out));

  // Notes on the sheet:
  //   Immediate Instructions are hardwired based upon OPCODE
  //   Func Codes need to be adjusted to match alu logic
  //   Add : 010
  //   Sub: 110
endmodule

module InstructionMemory (
  input  [15:0] InstrAddress,
  input  WriteEnable,
  input  [15:0] DataIn,
  input  ReadEnable,
  input  Clock,
  output [15:0] InstructionOutput
);

  RAM #(.addrWidth(16), .dataWidth(16)) ram_1 (
    .addr(InstrAddress), .we(WriteEnable), .oe(ReadEnable), .clk(Clock), .din(DataIn),
    .dout(InstructionOutput));
endmodule

module DataMemory (
  input  [7:0] Address,
  input  WriteEnable,
  input  Clock,
  input  [7:0] WriteData,
  output [7:0] ReadData
);

  wire comparator_1_eq, not_1_out;
  wire [7:0] ram_1_dout, register_1_q, register_2_q;

  not not_1 (not_1_out, WriteEnable);
  Register register_1 (.D(Address), .en(1'b1), .clk(Clock), .Q(register_1_q));  // open: clr
  RAM ram_1 (.addr(Address), .we(WriteEnable), .oe(not_1_out), .clk(Clock), .din(WriteData), .dout(ram_1_dout));
  Register register_2 (.D(WriteData), .en(1'b1), .clk(Clock), .Q(register_2_q));  // open: clr
  Comparator comparator_1 (.a(register_1_q), .b(Address), .eq(comparator_1_eq));  // open: gt, lt
  Multiplexer #(.width(8)) multiplexer_1 (.in0(ram_1_dout), .in1(register_2_q), .out(ReadData), .sel(comparator_1_eq));

  // Notes on the sheet:
  //   This Register System is a fix to the latency issue of writing to a data address and then trying to read it in the very next cycle
endmodule
